# Fritzing sketch LED (saved by Fritzing 0.9.2b)
breadboards: 1

parts:
  Raspberry_Pi_3 = Raspberry Pi 2
  S1 = Pushbutton [package="[THT]"]
  LED1 = RGB LED (com. cathode, rgb) [package="5 mm [THT]"]
  R1 = Resistor [tolerance=±5% resistance=220 package=THT]
  R2 = Resistor [tolerance=±5% resistance=220 package=THT]
  R3 = Resistor [tolerance=±5% resistance=220 package=THT]

nets:
  N1: Raspberry_Pi_3.GPIO17, R1.Pin_0
  N2: Raspberry_Pi_3.GPIO27, R2.Pin_0
  N3: Raspberry_Pi_3.GPIO22, R3.Pin_0
  N4: Raspberry_Pi_3.GND, S1.Pin_1, S1.Pin_2, LED1.common_cathode
  N5: Raspberry_Pi_3.GPIO26, S1.Pin_3, S1.Pin_4
  N6: LED1.red_anode, R1.Pin_1
  N7: LED1.green_anode, R2.Pin_1
  N8: LED1.blue_anode, R3.Pin_1
